// Logisim project main.circ as structural Verilog: 8 circuits, main circuit engine with controls
module _32_32_buffer (
  input  [31:0] Input_row,
  input  Write_row,
  input  [4:0] Row_selector,
  output [31:0] Row_0,
  output [31:0] Row_1,
  output [31:0] Row_2,
  output [31:0] Row_3,
  output [31:0] Row_4,
  output [31:0] Row_5,
  output [31:0] Row_6,
  output [31:0] Row_7,
  output [31:0] Row_8,
  output [31:0] Row_9,
  output [31:0] Row_10,
  output [31:0] Row_11,
  output [31:0] Row_12,
  output [31:0] Row_13,
  output [31:0] Row_14,
  output [31:0] Row_15,
  output [31:0] Row_16,
  output [31:0] Row_17,
  output [31:0] Row_18,
  output [31:0] Row_19,
  output [31:0] Row_20,
  output [31:0] Row_21,
  output [31:0] Row_22,
  output [31:0] Row_23,
  output [31:0] Row_24,
  output [31:0] Row_25,
  output [31:0] Row_26,
  output [31:0] Row_27,
  output [31:0] Row_28,
  output [31:0] Row_29,
  output [31:0] Row_30,
  output [31:0] Row_31
);

  wire decoder_1_out0, decoder_1_out1, decoder_1_out2, decoder_1_out3, decoder_1_out4, decoder_1_out5,
       decoder_1_out6, decoder_1_out7, decoder_1_out8, decoder_1_out9, decoder_1_out10, decoder_1_out11,
       decoder_1_out12, decoder_1_out13, decoder_1_out14, decoder_1_out15, decoder_1_out16, decoder_1_out17,
       decoder_1_out18, decoder_1_out19, decoder_1_out20, decoder_1_out21, decoder_1_out22, decoder_1_out23,
       decoder_1_out24, decoder_1_out25, decoder_1_out26, decoder_1_out27, decoder_1_out28, decoder_1_out29,
       decoder_1_out30, decoder_1_out31;

  Decoder #(.select(5), .disabled(0)) decoder_1 (
    .out0(decoder_1_out0), .out1(decoder_1_out1), .out2(decoder_1_out2), .out3(decoder_1_out3),
    .out4(decoder_1_out4), .out5(decoder_1_out5), .out6(decoder_1_out6), .out7(decoder_1_out7),
    .out8(decoder_1_out8), .out9(decoder_1_out9), .out10(decoder_1_out10), .out11(decoder_1_out11),
    .out12(decoder_1_out12), .out13(decoder_1_out13), .out14(decoder_1_out14), .out15(decoder_1_out15),
    .out16(decoder_1_out16), .out17(decoder_1_out17), .out18(decoder_1_out18), .out19(decoder_1_out19),
    .out20(decoder_1_out20), .out21(decoder_1_out21), .out22(decoder_1_out22), .out23(decoder_1_out23),
    .out24(decoder_1_out24), .out25(decoder_1_out25), .out26(decoder_1_out26), .out27(decoder_1_out27),
    .out28(decoder_1_out28), .out29(decoder_1_out29), .out30(decoder_1_out30), .out31(decoder_1_out31),
    .sel(Row_selector), .en(Write_row));
  Register #(.width(32)) register_1 (.D(Input_row), .Q(Row_0), .clk(decoder_1_out0));  // open: en, clr
  Register #(.width(32)) register_2 (.D(Input_row), .Q(Row_1), .clk(decoder_1_out1));  // open: en, clr
  Register #(.width(32)) register_3 (.D(Input_row), .Q(Row_2), .clk(decoder_1_out2));  // open: en, clr
  Register #(.width(32)) register_4 (.D(Input_row), .Q(Row_3), .clk(decoder_1_out3));  // open: en, clr
  Register #(.width(32)) register_5 (.D(Input_row), .Q(Row_4), .clk(decoder_1_out4));  // open: en, clr
  Register #(.width(32)) register_6 (.D(Input_row), .Q(Row_5), .clk(decoder_1_out5));  // open: en, clr
  Register #(.width(32)) register_7 (.D(Input_row), .Q(Row_6), .clk(decoder_1_out6));  // open: en, clr
  Register #(.width(32)) register_8 (.D(Input_row), .Q(Row_7), .clk(decoder_1_out7));  // open: en, clr
  Register #(.width(32)) register_9 (.D(Input_row), .Q(Row_8), .clk(decoder_1_out8));  // open: en, clr
  Register #(.width(32)) register_10 (.D(Input_row), .Q(Row_9), .clk(decoder_1_out9));  // open: en, clr
  Register #(.width(32)) register_11 (.D(Input_row), .Q(Row_10), .clk(decoder_1_out10));  // open: en, clr
  Register #(.width(32)) register_12 (.D(Input_row), .Q(Row_11), .clk(decoder_1_out11));  // open: en, clr
  Register #(.width(32)) register_13 (.D(Input_row), .Q(Row_12), .clk(decoder_1_out12));  // open: en, clr
  Register #(.width(32)) register_14 (.D(Input_row), .Q(Row_13), .clk(decoder_1_out13));  // open: en, clr
  Register #(.width(32)) register_15 (.D(Input_row), .Q(Row_14), .clk(decoder_1_out14));  // open: en, clr
  Register #(.width(32)) register_16 (.D(Input_row), .Q(Row_15), .clk(decoder_1_out15));  // open: en, clr
  Register #(.width(32)) register_17 (.D(Input_row), .Q(Row_16), .clk(decoder_1_out16));  // open: en, clr
  Register #(.width(32)) register_18 (.D(Input_row), .Q(Row_17), .clk(decoder_1_out17));  // open: en, clr
  Register #(.width(32)) register_19 (.D(Input_row), .Q(Row_18), .clk(decoder_1_out18));  // open: en, clr
  Register #(.width(32)) register_20 (.D(Input_row), .Q(Row_19), .clk(decoder_1_out19));  // open: en, clr
  Register #(.width(32)) register_21 (.D(Input_row), .Q(Row_20), .clk(decoder_1_out20));  // open: en, clr
  Register #(.width(32)) register_22 (.D(Input_row), .Q(Row_21), .clk(decoder_1_out21));  // open: en, clr
  Register #(.width(32)) register_23 (.D(Input_row), .Q(Row_22), .clk(decoder_1_out22));  // open: en, clr
  Register #(.width(32)) register_24 (.D(Input_row), .Q(Row_23), .clk(decoder_1_out23));  // open: en, clr
  Register #(.width(32)) register_25 (.D(Input_row), .Q(Row_24), .clk(decoder_1_out24));  // open: en, clr
  Register #(.width(32)) register_26 (.D(Input_row), .Q(Row_25), .clk(decoder_1_out25));  // open: en, clr
  Register #(.width(32)) register_27 (.D(Input_row), .Q(Row_26), .clk(decoder_1_out26));  // open: en, clr
  Register #(.width(32)) register_28 (.D(Input_row), .Q(Row_27), .clk(decoder_1_out27));  // open: en, clr
  Register #(.width(32)) register_29 (.D(Input_row), .Q(Row_28), .clk(decoder_1_out28));  // open: en, clr
  Register #(.width(32)) register_30 (.D(Input_row), .Q(Row_29), .clk(decoder_1_out29));  // open: en, clr
  Register #(.width(32)) register_31 (.D(Input_row), .Q(Row_30), .clk(decoder_1_out30));  // open: en, clr
  Register #(.width(32)) register_32 (.D(Input_row), .Q(Row_31), .clk(decoder_1_out31));  // open: en, clr

  // Other names for the same wires on the sheet: row0[31:0] = Row_0; row1[31:0] = Row_1; row2[31:0] = Row_2;
  //   row3[31:0] = Row_3; row4[31:0] = Row_4; row5[31:0] = Row_5; row6[31:0] = Row_6; row7[31:0] = Row_7;
  //   row8[31:0] = Row_8; row9[31:0] = Row_9; row10[31:0] = Row_10; row11[31:0] = Row_11; row12[31:0] = Row_12;
  //   row13[31:0] = Row_13; row14[31:0] = Row_14; row15[31:0] = Row_15; row16[31:0] = Row_16; row17[31:0] = Row_17;
  //   row18[31:0] = Row_18; row19[31:0] = Row_19; row20[31:0] = Row_20; row21[31:0] = Row_21; row22[31:0] = Row_22;
  //   row23[31:0] = Row_23; row24[31:0] = Row_24; row25[31:0] = Row_25; row26[31:0] = Row_26; row27[31:0] = Row_27;
  //   row28[31:0] = Row_28; row29[31:0] = Row_29; row30[31:0] = Row_30; row31[31:0] = Row_31
endmodule

module Keyboard_controller (
  input  [6:0] ASCII_code,
  output [4:0] Y,
  output [4:0] X,
  output Switch
);

  wire _0x0y, _0x0y_A, _0x_y, _0x_y_A, _0x_y_A_t, _0x_y_t, minus_x0y, minus_x0y_A, minus_x_y, minus_x_y_A,
       minus_x_y_A_t, minus_x_y_t, or_1_out, or_2_out, or_3_out, or_4_out, or_5_out, or_6_out, or_7_out,
       or_8_out, or_9_out, or_10_out, or_11_out, or_12_out, or_13_out, or_14_out, or_15_out, or_16_out,
       or_17_out, or_18_out, plus_x0y, plus_x0y_A, plus_x_y, plus_x_y_A, plus_x_y_A_t, plus_x_y_t;
  wire [4:0] counter_2_q;

  Comparator #(.width(7)) comparator_1 (.a(ASCII_code), .b(7'b0110111), .eq(plus_x_y_t));  // open: gt, lt
  Comparator #(.width(7)) comparator_2 (.a(ASCII_code), .b(7'b0110100), .eq(plus_x0y));  // open: gt, lt
  Comparator #(.width(7)) comparator_3 (.a(ASCII_code), .b(7'b0110001), .eq(plus_x_y));  // open: gt, lt
  Comparator #(.width(7)) comparator_4 (.a(ASCII_code), .b(7'b1110001), .eq(plus_x_y_A_t));  // open: gt, lt
  Comparator #(.width(7)) comparator_5 (.a(ASCII_code), .b(7'b1100001), .eq(plus_x0y_A));  // open: gt, lt
  Comparator #(.width(7)) comparator_6 (.a(ASCII_code), .b(7'b1111010), .eq(plus_x_y_A));  // open: gt, lt
  Comparator #(.width(7)) comparator_7 (.a(ASCII_code), .b(7'b0111000), .eq(_0x_y_t));  // open: gt, lt
  Comparator #(.width(7)) comparator_8 (.a(ASCII_code), .b(7'b0110101), .eq(_0x0y));  // open: gt, lt
  Comparator #(.width(7)) comparator_9 (.a(ASCII_code), .b(7'b0110010), .eq(_0x_y));  // open: gt, lt
  Comparator #(.width(7)) comparator_10 (.a(ASCII_code), .b(7'b1110111), .eq(_0x_y_A_t));  // open: gt, lt
  Comparator #(.width(7)) comparator_11 (.a(ASCII_code), .b(7'b0100000), .eq(_0x0y_A));  // open: gt, lt
  Comparator #(.width(7)) comparator_12 (.a(ASCII_code), .b(7'b1110011), .eq(_0x_y_A));  // open: gt, lt
  Comparator #(.width(7)) comparator_13 (.a(ASCII_code), .b(7'b0111001), .eq(minus_x_y_t));  // open: gt, lt
  Comparator #(.width(7)) comparator_14 (.a(ASCII_code), .b(7'b0110110), .eq(minus_x0y));  // open: gt, lt
  Comparator #(.width(7)) comparator_15 (.a(ASCII_code), .b(7'b0110011), .eq(minus_x_y));  // open: gt, lt
  Comparator #(.width(7)) comparator_16 (.a(ASCII_code), .b(7'b1100101), .eq(minus_x_y_A_t));  // open: gt, lt
  Comparator #(.width(7)) comparator_17 (.a(ASCII_code), .b(7'b1100100), .eq(minus_x0y_A));  // open: gt, lt
  Comparator #(.width(7)) comparator_18 (.a(ASCII_code), .b(7'b1100011), .eq(minus_x_y_A));  // open: gt, lt
  or or_1 (or_1_out, minus_x_y_t, minus_x_y_A_t);
  or or_2 (or_2_out, _0x_y_t, _0x_y_A_t);
  or or_3 (or_3_out, plus_x_y_t, plus_x_y_A_t);
  or or_4 (or_4_out, minus_x_y, minus_x_y_A);
  or or_5 (or_5_out, _0x_y, _0x_y_A);
  or or_6 (or_6_out, plus_x_y, plus_x_y_A);
  or or_7 (or_7_out, minus_x_y_t, minus_x_y_A_t);
  or or_8 (or_8_out, minus_x0y, minus_x0y_A);
  or or_9 (or_9_out, minus_x_y, minus_x_y_A);
  or or_10 (or_10_out, plus_x_y_t, plus_x_y_A_t);
  or or_11 (or_11_out, plus_x0y, plus_x0y_A);
  or or_12 (or_12_out, plus_x_y, plus_x_y_A);
  or or_13 (or_13_out, or_1_out, or_2_out, or_3_out);
  or or_14 (or_14_out, or_13_out, or_15_out);
  or or_15 (or_15_out, or_4_out, or_5_out, or_6_out);
  or or_16 (or_16_out, or_7_out, or_8_out, or_9_out);
  or or_17 (or_17_out, or_16_out, or_18_out);
  or or_18 (or_18_out, or_10_out, or_11_out, or_12_out);
  // Probe on Y
  Counter #(.width(5), .max('h1f)) counter_1 (
    .load(or_13_out), .count(or_14_out), .Q(Y), .clk(or_14_out));  // open: D, carry, clr
  Counter #(.width(5), .max('h1f)) counter_2 (
    .load(or_16_out), .count(or_17_out), .Q(counter_2_q), .clk(or_17_out));  // open: D, carry, clr
  // Probe on X
  Adder #(.width(5)) adder_1 (.a({5{1'b1}}), .b(counter_2_q), .out(X));  // open: cin, cout
  or or_19 (Switch, _0x0y, _0x0y_A);

  // Notes on the sheet:
  //   Y position
  //   X position
endmodule

module SELECT (
  input  [31:0] Input1,
  input  Switch,
  input  [31:0] Input2,
  output [31:0] Output
);

  Multiplexer #(.width(32), .disabled(0), .enable("false")) multiplexer_1 (
    .in0(Input1), .in1(Input2), .out(Output), .sel(Switch));
endmodule

module bit_invertor (
  input  [31:0] INPUT9,
  input  [31:0] INPUT1,
  input  [31:0] INPUT10,
  input  [31:0] INPUT17,
  input  [31:0] INPUT2,
  input  [31:0] INPUT11,
  input  [31:0] INPUT18,
  input  [31:0] INPUT25,
  input  [31:0] INPUT3,
  input  [31:0] INPUT12,
  input  [31:0] INPUT19,
  input  [31:0] INPUT26,
  input  [31:0] INPUT4,
  input  SWITCH,
  input  [31:0] INPUT13,
  input  [31:0] INPUT20,
  input  [31:0] INPUT27,
  input  [4:0] Y,
  input  [31:0] INPUT5,
  input  [4:0] X,
  input  [31:0] INPUT14,
  input  [31:0] INPUT21,
  input  [31:0] INPUT28,
  input  [31:0] INPUT6,
  input  [31:0] INPUT15,
  input  [31:0] INPUT22,
  input  [31:0] INPUT29,
  input  [31:0] INPUT7,
  input  [31:0] INPUT16,
  input  [31:0] INPUT23,
  input  [31:0] INPUT30,
  input  [31:0] INPUT8,
  input  [31:0] INPUT24,
  input  [31:0] INPUT31,
  input  [31:0] INPUT32,
  output [31:0] CHANGED_STRING,
  output [31:0] OUTPUT1,
  output [31:0] OUTPUT2,
  output [31:0] OUTPUT3,
  output [31:0] OUTPUT4,
  output [31:0] OUTPUT5,
  output [31:0] OUTPUT6,
  output [31:0] OUTPUT7,
  output [31:0] OUTPUT8,
  output [31:0] OUTPUT9,
  output [31:0] OUTPUT10,
  output [31:0] OUTPUT11,
  output [31:0] OUTPUT12,
  output [31:0] OUTPUT13,
  output [31:0] OUTPUT14,
  output [31:0] OUTPUT15,
  output [31:0] OUTPUT16,
  output [31:0] OUTPUT17,
  output [31:0] OUTPUT18,
  output [31:0] OUTPUT19,
  output [31:0] OUTPUT20,
  output [31:0] OUTPUT21,
  output [31:0] OUTPUT22,
  output [31:0] OUTPUT23,
  output [31:0] OUTPUT24,
  output [31:0] OUTPUT25,
  output [31:0] OUTPUT26,
  output [31:0] OUTPUT27,
  output [31:0] OUTPUT28,
  output [31:0] OUTPUT29,
  output [31:0] OUTPUT30,
  output [31:0] OUTPUT31,
  output [31:0] OUTPUT32
);

  wire decoder_2_out0, decoder_2_out1, decoder_2_out2, decoder_2_out3, decoder_2_out4, decoder_2_out5,
       decoder_2_out6, decoder_2_out7, decoder_2_out8, decoder_2_out9, decoder_2_out10, decoder_2_out11,
       decoder_2_out12, decoder_2_out13, decoder_2_out14, decoder_2_out15, decoder_2_out16, decoder_2_out17,
       decoder_2_out18, decoder_2_out19, decoder_2_out20, decoder_2_out21, decoder_2_out22, decoder_2_out23,
       decoder_2_out24, decoder_2_out25, decoder_2_out26, decoder_2_out27, decoder_2_out28, decoder_2_out29,
       decoder_2_out30, decoder_2_out31;
  wire [31:0] decoder_1_out0, multiplexer_1_out, select_22_output, select_23_output, select_24_output,
       select_25_output, select_26_output, select_27_output, select_28_output, select_29_output,
       select_30_output, select_31_output, select_32_output, select_33_output, select_34_output,
       select_35_output, select_36_output, select_37_output, select_38_output, select_39_output,
       select_40_output, select_41_output, select_42_output, select_43_output, select_44_output,
       select_45_output, select_46_output, select_47_output, select_48_output, select_49_output,
       select_50_output, select_51_output, select_52_output, select_53_output, xor_1_out;

  SELECT select_1 (.Input1(INPUT1), .Switch(SWITCH), .Input2(select_22_output), .Output(OUTPUT1));
  SELECT select_2 (.Input1(INPUT2), .Switch(SWITCH), .Input2(select_23_output), .Output(OUTPUT2));
  SELECT select_3 (.Input1(INPUT3), .Switch(SWITCH), .Input2(select_24_output), .Output(OUTPUT3));
  SELECT select_4 (.Input1(INPUT4), .Switch(SWITCH), .Input2(select_25_output), .Output(OUTPUT4));
  SELECT select_5 (.Input1(INPUT5), .Switch(SWITCH), .Input2(select_26_output), .Output(OUTPUT5));
  SELECT select_6 (.Input1(INPUT6), .Switch(SWITCH), .Input2(select_27_output), .Output(OUTPUT6));
  SELECT select_7 (.Input1(INPUT7), .Switch(SWITCH), .Input2(select_28_output), .Output(OUTPUT7));
  SELECT select_8 (.Input1(INPUT8), .Switch(SWITCH), .Input2(select_29_output), .Output(OUTPUT8));
  SELECT select_9 (.Input1(INPUT9), .Switch(SWITCH), .Input2(select_30_output), .Output(OUTPUT9));
  SELECT select_10 (.Input1(INPUT10), .Switch(SWITCH), .Input2(select_31_output), .Output(OUTPUT10));
  SELECT select_11 (.Input1(INPUT11), .Switch(SWITCH), .Input2(select_32_output), .Output(OUTPUT11));
  Multiplexer #(.select(5), .width(32), .enable("false")) multiplexer_1 (
    .in0(INPUT1), .in1(INPUT2), .in2(INPUT3), .in3(INPUT4), .in4(INPUT5), .in5(INPUT6), .in6(INPUT7),
    .in7(INPUT8), .in8(INPUT9), .in9(INPUT10), .in10(INPUT11), .in11(INPUT12), .in12(INPUT13),
    .in13(INPUT14), .in14(INPUT15), .in15(INPUT16), .in16(INPUT17), .in17(INPUT18), .in18(INPUT19),
    .in19(INPUT20), .in20(INPUT21), .in21(INPUT22), .in22(INPUT23), .in23(INPUT24), .in24(INPUT25),
    .in25(INPUT26), .in26(INPUT27), .in27(INPUT28), .in28(INPUT29), .in29(INPUT30), .in30(INPUT31),
    .in31(INPUT32), .out(multiplexer_1_out), .sel(Y));
  SELECT select_12 (.Input1(INPUT12), .Switch(SWITCH), .Input2(select_33_output), .Output(OUTPUT12));
  Decoder #(.select(5), .disabled(0)) decoder_1 (
    .out0(decoder_1_out0[0]), .out1(decoder_1_out0[1]), .out2(decoder_1_out0[2]), .out3(decoder_1_out0[3]),
    .out4(decoder_1_out0[4]), .out5(decoder_1_out0[5]), .out6(decoder_1_out0[6]), .out7(decoder_1_out0[7]),
    .out8(decoder_1_out0[8]), .out9(decoder_1_out0[9]), .out10(decoder_1_out0[10]),
    .out11(decoder_1_out0[11]), .out12(decoder_1_out0[12]), .out13(decoder_1_out0[13]),
    .out14(decoder_1_out0[14]), .out15(decoder_1_out0[15]), .out16(decoder_1_out0[16]),
    .out17(decoder_1_out0[17]), .out18(decoder_1_out0[18]), .out19(decoder_1_out0[19]),
    .out20(decoder_1_out0[20]), .out21(decoder_1_out0[21]), .out22(decoder_1_out0[22]),
    .out23(decoder_1_out0[23]), .out24(decoder_1_out0[24]), .out25(decoder_1_out0[25]),
    .out26(decoder_1_out0[26]), .out27(decoder_1_out0[27]), .out28(decoder_1_out0[28]),
    .out29(decoder_1_out0[29]), .out30(decoder_1_out0[30]), .out31(decoder_1_out0[31]), .sel(X), .en(SWITCH));
  Decoder #(.select(5), .disabled(0)) decoder_2 (
    .out0(decoder_2_out0), .out1(decoder_2_out1), .out2(decoder_2_out2), .out3(decoder_2_out3),
    .out4(decoder_2_out4), .out5(decoder_2_out5), .out6(decoder_2_out6), .out7(decoder_2_out7),
    .out8(decoder_2_out8), .out9(decoder_2_out9), .out10(decoder_2_out10), .out11(decoder_2_out11),
    .out12(decoder_2_out12), .out13(decoder_2_out13), .out14(decoder_2_out14), .out15(decoder_2_out15),
    .out16(decoder_2_out16), .out17(decoder_2_out17), .out18(decoder_2_out18), .out19(decoder_2_out19),
    .out20(decoder_2_out20), .out21(decoder_2_out21), .out22(decoder_2_out22), .out23(decoder_2_out23),
    .out24(decoder_2_out24), .out25(decoder_2_out25), .out26(decoder_2_out26), .out27(decoder_2_out27),
    .out28(decoder_2_out28), .out29(decoder_2_out29), .out30(decoder_2_out30), .out31(decoder_2_out31),
    .sel(Y), .en(SWITCH));
  SELECT select_13 (.Input1(INPUT13), .Switch(SWITCH), .Input2(select_34_output), .Output(OUTPUT13));
  SELECT select_14 (.Input1(INPUT14), .Switch(SWITCH), .Input2(select_35_output), .Output(OUTPUT14));
  assign xor_1_out = multiplexer_1_out ^ decoder_1_out0;  // XOR_Gate xor_1, 32 bits wide
  SELECT select_15 (.Input1(INPUT15), .Switch(SWITCH), .Input2(select_36_output), .Output(OUTPUT15));
  SELECT select_16 (.Input1(INPUT16), .Switch(SWITCH), .Input2(select_37_output), .Output(OUTPUT16));
  SELECT select_17 (.Input1(INPUT17), .Switch(SWITCH), .Input2(select_38_output), .Output(OUTPUT17));
  SELECT select_18 (.Input1(multiplexer_1_out), .Switch(SWITCH), .Input2(xor_1_out), .Output(CHANGED_STRING));
  SELECT select_19 (.Input1(INPUT18), .Switch(SWITCH), .Input2(select_39_output), .Output(OUTPUT18));
  SELECT select_20 (.Input1(INPUT19), .Switch(SWITCH), .Input2(select_40_output), .Output(OUTPUT19));
  SELECT select_21 (.Input1(INPUT20), .Switch(SWITCH), .Input2(select_41_output), .Output(OUTPUT20));
  SELECT select_22 (.Input1(INPUT1), .Switch(decoder_2_out0), .Input2(xor_1_out), .Output(select_22_output));
  SELECT select_23 (.Input1(INPUT2), .Switch(decoder_2_out1), .Input2(xor_1_out), .Output(select_23_output));
  SELECT select_24 (.Input1(INPUT3), .Switch(decoder_2_out2), .Input2(xor_1_out), .Output(select_24_output));
  SELECT select_25 (.Input1(INPUT4), .Switch(decoder_2_out3), .Input2(xor_1_out), .Output(select_25_output));
  SELECT select_26 (.Input1(INPUT5), .Switch(decoder_2_out4), .Input2(xor_1_out), .Output(select_26_output));
  SELECT select_27 (.Input1(INPUT6), .Switch(decoder_2_out5), .Input2(xor_1_out), .Output(select_27_output));
  SELECT select_28 (.Input1(INPUT7), .Switch(decoder_2_out6), .Input2(xor_1_out), .Output(select_28_output));
  SELECT select_29 (.Input1(INPUT8), .Switch(decoder_2_out7), .Input2(xor_1_out), .Output(select_29_output));
  SELECT select_30 (.Input1(INPUT9), .Switch(decoder_2_out8), .Input2(xor_1_out), .Output(select_30_output));
  SELECT select_31 (.Input1(INPUT10), .Switch(decoder_2_out9), .Input2(xor_1_out), .Output(select_31_output));
  SELECT select_32 (.Input1(INPUT11), .Switch(decoder_2_out10), .Input2(xor_1_out), .Output(select_32_output));
  SELECT select_33 (.Input1(INPUT12), .Switch(decoder_2_out11), .Input2(xor_1_out), .Output(select_33_output));
  SELECT select_34 (.Input1(INPUT13), .Switch(decoder_2_out12), .Input2(xor_1_out), .Output(select_34_output));
  SELECT select_35 (.Input1(INPUT14), .Switch(decoder_2_out13), .Input2(xor_1_out), .Output(select_35_output));
  SELECT select_36 (.Input1(INPUT15), .Switch(decoder_2_out14), .Input2(xor_1_out), .Output(select_36_output));
  SELECT select_37 (.Input1(INPUT16), .Switch(decoder_2_out15), .Input2(xor_1_out), .Output(select_37_output));
  SELECT select_38 (.Input1(INPUT17), .Switch(decoder_2_out16), .Input2(xor_1_out), .Output(select_38_output));
  SELECT select_39 (.Input1(INPUT18), .Switch(decoder_2_out17), .Input2(xor_1_out), .Output(select_39_output));
  SELECT select_40 (.Input1(INPUT19), .Switch(decoder_2_out18), .Input2(xor_1_out), .Output(select_40_output));
  SELECT select_41 (.Input1(INPUT20), .Switch(decoder_2_out19), .Input2(xor_1_out), .Output(select_41_output));
  SELECT select_42 (.Input1(INPUT21), .Switch(decoder_2_out20), .Input2(xor_1_out), .Output(select_42_output));
  SELECT select_43 (.Input1(INPUT22), .Switch(decoder_2_out21), .Input2(xor_1_out), .Output(select_43_output));
  SELECT select_44 (.Input1(INPUT23), .Switch(decoder_2_out22), .Input2(xor_1_out), .Output(select_44_output));
  SELECT select_45 (.Input1(INPUT24), .Switch(decoder_2_out23), .Input2(xor_1_out), .Output(select_45_output));
  SELECT select_46 (.Input1(INPUT25), .Switch(decoder_2_out24), .Input2(xor_1_out), .Output(select_46_output));
  SELECT select_47 (.Input1(INPUT26), .Switch(decoder_2_out25), .Input2(xor_1_out), .Output(select_47_output));
  SELECT select_48 (.Input1(INPUT27), .Switch(decoder_2_out26), .Input2(xor_1_out), .Output(select_48_output));
  SELECT select_49 (.Input1(INPUT28), .Switch(decoder_2_out27), .Input2(xor_1_out), .Output(select_49_output));
  SELECT select_50 (.Input1(INPUT29), .Switch(decoder_2_out28), .Input2(xor_1_out), .Output(select_50_output));
  SELECT select_51 (.Input1(INPUT30), .Switch(decoder_2_out29), .Input2(xor_1_out), .Output(select_51_output));
  SELECT select_52 (.Input1(INPUT31), .Switch(decoder_2_out30), .Input2(xor_1_out), .Output(select_52_output));
  SELECT select_53 (.Input1(INPUT32), .Switch(decoder_2_out31), .Input2(xor_1_out), .Output(select_53_output));
  SELECT select_54 (.Input1(INPUT21), .Switch(SWITCH), .Input2(select_42_output), .Output(OUTPUT21));
  SELECT select_55 (.Input1(INPUT22), .Switch(SWITCH), .Input2(select_43_output), .Output(OUTPUT22));
  SELECT select_56 (.Input1(INPUT23), .Switch(SWITCH), .Input2(select_44_output), .Output(OUTPUT23));
  SELECT select_57 (.Input1(INPUT24), .Switch(SWITCH), .Input2(select_45_output), .Output(OUTPUT24));
  SELECT select_58 (.Input1(INPUT25), .Switch(SWITCH), .Input2(select_46_output), .Output(OUTPUT25));
  SELECT select_59 (.Input1(INPUT26), .Switch(SWITCH), .Input2(select_47_output), .Output(OUTPUT26));
  SELECT select_60 (.Input1(INPUT27), .Switch(SWITCH), .Input2(select_48_output), .Output(OUTPUT27));
  SELECT select_61 (.Input1(INPUT28), .Switch(SWITCH), .Input2(select_49_output), .Output(OUTPUT28));
  SELECT select_62 (.Input1(INPUT29), .Switch(SWITCH), .Input2(select_50_output), .Output(OUTPUT29));
  SELECT select_63 (.Input1(INPUT30), .Switch(SWITCH), .Input2(select_51_output), .Output(OUTPUT30));
  SELECT select_64 (.Input1(INPUT31), .Switch(SWITCH), .Input2(select_52_output), .Output(OUTPUT31));
  SELECT select_65 (.Input1(INPUT32), .Switch(SWITCH), .Input2(select_53_output), .Output(OUTPUT32));
endmodule

module engine_with_controls (
  input  [7:0] birth_input,
  input  [7:0] survival_input
);

  wire and_1_out, and_2_out, and_3_out, and_4_out, and_5_out, and_6_out, and_7_out, and_10_out, and_11_out,
       and_12_out, and_13_out, and_14_out, cdm_8_mark5_1_p1, cdm_8_mark5_1_p2, cdm_8_mark5_1_p4,
       cdm_8_mark5_1_p5, cdm_8_mark5_1_p6, cdm_8_mark5_1_p7, cdm_8_mark5_1_p8, cdm_8_mark5_1_p9, change_bit,
       change_bit_slow, clock, code, comparator_1_eq, comparator_2_eq, comparator_3_eq, comparator_4_eq,
       comparator_5_eq, comparator_6_eq, comparator_7_eq, comparator_8_eq, comparator_9_eq, comparator_10_eq,
       comparator_11_lt, comparator_12_eq, comparator_13_eq, comparator_14_eq, comparator_15_eq,
       comparator_16_eq, CPU_invert_bit, CPU_invert_bit_slow, data, decoder_1_out0, decoder_3_out0,
       decoder_4_out1, decoder_6_out0, decoder_7_out1, decoder_9_out1, decoder_10_out1, decoder_11_out1,
       decoder_12_out1, decoder_13_out1, in_out, IOsel, is_null_byte, is_row_null, mem, multiplexer_1_out,
       multiplexer_4_out, not_2_out, not_3_out, not_4_out, not_5_out, not_6_out, not_7_out, not_8_out,
       not_9_out, not_11_out, not_12_out, not_13_out, not_15_out, not_16_out, not_17_out, not_18_out,
       not_20_out, not_21_out, not_22_out, not_23_out, not_24_out, not_25_out, not_26_out, not_28_out,
       not_29_out, not_30_out, not_31_out, playing, RAM, selected_bit, setting, start, update_generation,
       update_generation_slow, xnor_1_out, xnor_2_out, xnor_3_out;
  wire [4:0] cpuX, cpuY, keyboard_controller_1_x, keyboard_controller_1_y, multiplexer_2_out,
       multiplexer_3_out;
  wire [6:0] keyboard_1_data;
  wire [7:0] bus, cdm_8_mark5_1_p13, cdm_8_mark5_1_p14, controlled_buffer_1_out, controlled_buffer_3_out,
       env_sum, IOaddr, not_27_out, register_1_q, register_5_q, register_6_q;
  wire [7:1] register_3_q;
  wire [7:5] register_2_q, register_4_q;
  wire [31:0] bit_invertor_1_output1, bit_invertor_1_output2, bit_invertor_1_output3, bit_invertor_1_output4,
       bit_invertor_1_output5, bit_invertor_1_output6, bit_invertor_1_output7, bit_invertor_1_output8,
       bit_invertor_1_output9, bit_invertor_1_output10, bit_invertor_1_output11, bit_invertor_1_output12,
       bit_invertor_1_output13, bit_invertor_1_output14, bit_invertor_1_output15, bit_invertor_1_output16,
       bit_invertor_1_output17, bit_invertor_1_output18, bit_invertor_1_output19, bit_invertor_1_output20,
       bit_invertor_1_output21, bit_invertor_1_output22, bit_invertor_1_output23, bit_invertor_1_output24,
       bit_invertor_1_output25, bit_invertor_1_output26, bit_invertor_1_output27, bit_invertor_1_output28,
       bit_invertor_1_output29, bit_invertor_1_output30, bit_invertor_1_output31, bit_invertor_1_output32,
       generation_buffer_1_row_0_2, generation_buffer_1_row_1_2, generation_buffer_1_row_2_2,
       generation_buffer_1_row_3_2, generation_buffer_1_row_4_2, generation_buffer_1_row_5_2,
       generation_buffer_1_row_6_2, generation_buffer_1_row_7_2, generation_buffer_1_row_8_2,
       generation_buffer_1_row_9_2, generation_buffer_1_row_10_2, generation_buffer_1_row_11_2,
       generation_buffer_1_row_12_2, generation_buffer_1_row_13_2, generation_buffer_1_row_14_2,
       generation_buffer_1_row_15_2, generation_buffer_1_row_16_2, generation_buffer_1_row_17_2,
       generation_buffer_1_row_18_2, generation_buffer_1_row_19_2, generation_buffer_1_row_20_2,
       generation_buffer_1_row_21_2, generation_buffer_1_row_22_2, generation_buffer_1_row_23_2,
       generation_buffer_1_row_24_2, generation_buffer_1_row_25_2, generation_buffer_1_row_26_2,
       generation_buffer_1_row_27_2, generation_buffer_1_row_28_2, generation_buffer_1_row_29_2,
       generation_buffer_1_row_30_2, generation_buffer_1_row_31_2, inverted_row, n32_32_buffer_1_row_0,
       n32_32_buffer_1_row_1, n32_32_buffer_1_row_2, n32_32_buffer_1_row_3, n32_32_buffer_1_row_4,
       n32_32_buffer_1_row_5, n32_32_buffer_1_row_6, n32_32_buffer_1_row_7, n32_32_buffer_1_row_8,
       n32_32_buffer_1_row_9, n32_32_buffer_1_row_10, n32_32_buffer_1_row_11, n32_32_buffer_1_row_12,
       n32_32_buffer_1_row_13, n32_32_buffer_1_row_14, n32_32_buffer_1_row_15, n32_32_buffer_1_row_16,
       n32_32_buffer_1_row_17, n32_32_buffer_1_row_18, n32_32_buffer_1_row_19, n32_32_buffer_1_row_20,
       n32_32_buffer_1_row_21, n32_32_buffer_1_row_22, n32_32_buffer_1_row_23, n32_32_buffer_1_row_24,
       n32_32_buffer_1_row_25, n32_32_buffer_1_row_26, n32_32_buffer_1_row_27, n32_32_buffer_1_row_28,
       n32_32_buffer_1_row_29, n32_32_buffer_1_row_30, n32_32_buffer_1_row_31;

  Keyboard keyboard_1 (.clk(clock), .re(setting), .data(keyboard_1_data));  // open: clr, avail
  Button u_Start (.out(start));
  Keyboard_controller keyboard_controller_1 (
    .ASCII_code(keyboard_1_data), .X(keyboard_controller_1_x), .Y(keyboard_controller_1_y),
    .Switch(change_bit));
  // Probe on keyboard_controller_1_y
  // Probe on keyboard_controller_1_x
  not not_1 (change_bit_slow, not_2_out);
  not not_2 (not_2_out, change_bit);
  not not_3 (not_3_out, not_3_out);
  not not_4 (not_4_out, not_4_out);
  not not_5 (not_5_out, not_5_out);
  not not_6 (not_6_out, not_6_out);
  Multiplexer #(.disabled(0), .enable("false")) multiplexer_1 (
    .in0(change_bit), .in1(CPU_invert_bit), .out(multiplexer_1_out), .sel(playing));
  // Probe on multiplexer_2_out
  Multiplexer #(.width(5), .disabled(0), .enable("false")) multiplexer_2 (
    .in0(cpuY), .in1(keyboard_controller_1_y), .out(multiplexer_2_out), .sel(setting));
  Multiplexer #(.width(5), .disabled(0), .enable("false")) multiplexer_3 (
    .in0(keyboard_controller_1_x), .in1(cpuX), .out(multiplexer_3_out), .sel(playing));
  // Probe on multiplexer_3_out
  not not_7 (not_7_out, start);
  _32_32_buffer u_32_32_buffer_1 (
    .Row_0(n32_32_buffer_1_row_0), .Row_1(n32_32_buffer_1_row_1), .Row_2(n32_32_buffer_1_row_2),
    .Row_3(n32_32_buffer_1_row_3), .Row_4(n32_32_buffer_1_row_4), .Row_5(n32_32_buffer_1_row_5),
    .Row_6(n32_32_buffer_1_row_6), .Row_7(n32_32_buffer_1_row_7), .Row_8(n32_32_buffer_1_row_8),
    .Row_9(n32_32_buffer_1_row_9), .Row_10(n32_32_buffer_1_row_10), .Row_11(n32_32_buffer_1_row_11),
    .Row_12(n32_32_buffer_1_row_12), .Row_13(n32_32_buffer_1_row_13), .Row_14(n32_32_buffer_1_row_14),
    .Row_15(n32_32_buffer_1_row_15), .Row_16(n32_32_buffer_1_row_16), .Row_17(n32_32_buffer_1_row_17),
    .Row_18(n32_32_buffer_1_row_18), .Row_19(n32_32_buffer_1_row_19), .Row_20(n32_32_buffer_1_row_20),
    .Row_21(n32_32_buffer_1_row_21), .Row_22(n32_32_buffer_1_row_22), .Row_23(n32_32_buffer_1_row_23),
    .Row_24(n32_32_buffer_1_row_24), .Row_25(n32_32_buffer_1_row_25), .Row_26(n32_32_buffer_1_row_26),
    .Row_27(n32_32_buffer_1_row_27), .Row_28(n32_32_buffer_1_row_28), .Row_29(n32_32_buffer_1_row_29),
    .Row_30(n32_32_buffer_1_row_30), .Row_31(n32_32_buffer_1_row_31), .Row_selector(multiplexer_2_out),
    .Write_row(multiplexer_1_out), .Input_row(inverted_row));
  Register register_1 (.D(bus), .Q(register_1_q), .clk(not_9_out));  // open: en, clr
  not not_8 (not_8_out, decoder_1_out0);
  not not_9 (not_9_out, not_8_out);
  not not_10 (CPU_invert_bit_slow, not_11_out);
  not not_11 (not_11_out, CPU_invert_bit);
  assign controlled_buffer_1_out = decoder_3_out0 ? bus : 8'bz;  // Controlled_Buffer controlled_buffer_1
  Register register_2 (.D(controlled_buffer_1_out), .Q({register_2_q, cpuY}), .clk(not_12_out));  // open: en, clr
  not not_12 (not_12_out, not_13_out);
  Register register_3 (.D(8'h1), .Q({register_3_q, playing}), .clk(xnor_1_out));  // open: en, clr
  xnor xnor_1 (xnor_1_out, not_7_out, start);
  Decoder #(.disabled(0)) decoder_1 (.out0(decoder_1_out0), .sel(in_out), .en(and_1_out));  // open: out1
  Decoder #(.disabled(0)) decoder_2 (.out0(CPU_invert_bit), .sel(in_out), .en(and_2_out));  // open: out1
  Decoder #(.disabled(0)) decoder_3 (.out0(decoder_3_out0), .sel(in_out), .en(and_3_out));  // open: out1
  not not_13 (not_13_out, decoder_3_out0);
  Decoder #(.disabled(0)) decoder_4 (.out1(decoder_4_out1), .sel(in_out), .en(and_4_out));  // open: out0
  assign bus = decoder_4_out1 ? {register_3_q, playing} : 8'bz;  // Controlled_Buffer controlled_buffer_2
  tiny_bit_invertor tiny_bit_invertor_1 (
    .Row_0(n32_32_buffer_1_row_0), .Row_1(n32_32_buffer_1_row_1), .Row_2(n32_32_buffer_1_row_2),
    .Row_3(n32_32_buffer_1_row_3), .Row_4(n32_32_buffer_1_row_4), .Row_5(n32_32_buffer_1_row_5),
    .Row_6(n32_32_buffer_1_row_6), .Row_7(n32_32_buffer_1_row_7), .Row_8(n32_32_buffer_1_row_8),
    .Row_9(n32_32_buffer_1_row_9), .Row_10(n32_32_buffer_1_row_10), .Row_11(n32_32_buffer_1_row_11),
    .Row_12(n32_32_buffer_1_row_12), .Row_13(n32_32_buffer_1_row_13), .Row_14(n32_32_buffer_1_row_14),
    .Row_15(n32_32_buffer_1_row_15), .Row_16(n32_32_buffer_1_row_16), .Row_17(n32_32_buffer_1_row_17),
    .Row_18(n32_32_buffer_1_row_18), .Row_19(n32_32_buffer_1_row_19), .Row_20(n32_32_buffer_1_row_20),
    .Row_21(n32_32_buffer_1_row_21), .Row_22(n32_32_buffer_1_row_22), .Row_23(n32_32_buffer_1_row_23),
    .Row_24(n32_32_buffer_1_row_24), .Row_25(n32_32_buffer_1_row_25), .Row_26(n32_32_buffer_1_row_26),
    .Row_27(n32_32_buffer_1_row_27), .Row_28(n32_32_buffer_1_row_28), .Row_29(n32_32_buffer_1_row_29),
    .Row_30(n32_32_buffer_1_row_30), .Row_31(n32_32_buffer_1_row_31), .Row_with_inverted_bit(inverted_row),
    .Y__row_index(multiplexer_2_out), .X__bit_index(multiplexer_3_out));
  Comparator comparator_1 (.a(IOaddr), .b({8{1'b1}}), .eq(comparator_1_eq));  // open: gt, lt
  and and_1 (and_1_out, comparator_1_eq, IOsel);
  Comparator comparator_2 (.a(IOaddr), .b(8'hf9), .eq(comparator_2_eq));  // open: gt, lt
  and and_2 (and_2_out, comparator_2_eq, IOsel);
  Comparator comparator_3 (.a(IOaddr), .b(8'hf3), .eq(comparator_3_eq));  // open: gt, lt
  and and_3 (and_3_out, comparator_3_eq, IOsel);
  Comparator comparator_4 (.a(IOaddr), .b(8'hf0), .eq(comparator_4_eq));  // open: gt, lt
  and and_4 (and_4_out, comparator_4_eq, IOsel);
  not not_14 (setting, playing);
  not not_15 (not_15_out, not_15_out);
  // Probe on inverted_row
  not not_16 (not_16_out, not_16_out);
  not not_17 (not_17_out, not_17_out);
  LED led_1 (.in(comparator_5_eq));
  Comparator comparator_5 (.a(8'h40), .b(register_1_q), .eq(comparator_5_eq));  // open: gt, lt
  LED led_2 (.in(comparator_6_eq));
  Comparator comparator_6 (.a(8'h41), .b(register_1_q), .eq(comparator_6_eq));  // open: gt, lt
  Comparator comparator_7 (.a(8'h42), .b(register_1_q), .eq(comparator_7_eq));  // open: gt, lt
  not not_18 (not_18_out, setting);
  LED led_3 (.in(comparator_7_eq));
  assign controlled_buffer_3_out = decoder_6_out0 ? bus : 8'bz;  // Controlled_Buffer controlled_buffer_3
  xnor xnor_2 (xnor_2_out, not_18_out, setting);
  not not_19 (update_generation_slow, not_20_out);
  not not_20 (not_20_out, update_generation);
  Register register_4 (.D(controlled_buffer_3_out), .Q({register_4_q, cpuX}), .clk(not_22_out));  // open: en, clr
  not not_21 (not_21_out, decoder_6_out0);
  not not_22 (not_22_out, not_21_out);
  assign bus = decoder_7_out1 ? register_5_q : 8'bz;  // Controlled_Buffer controlled_buffer_4
  Register register_5 (.D(birth_input), .Q(register_5_q), .clk(xnor_2_out));  // open: en, clr
  generation_buffer generation_buffer_1 (
    .Save_generation_trigger(multiplexer_4_out), .Row_0(n32_32_buffer_1_row_0),
    .Row_1(n32_32_buffer_1_row_1), .Row_2(n32_32_buffer_1_row_2), .Row_3(n32_32_buffer_1_row_3),
    .Row_4(n32_32_buffer_1_row_4), .Row_5(n32_32_buffer_1_row_5), .Row_6(n32_32_buffer_1_row_6),
    .Row_7(n32_32_buffer_1_row_7), .Row_8(n32_32_buffer_1_row_8), .Row_9(n32_32_buffer_1_row_9),
    .Row_10(n32_32_buffer_1_row_10), .Row_11(n32_32_buffer_1_row_11), .Row_12(n32_32_buffer_1_row_12),
    .Row_13(n32_32_buffer_1_row_13), .Row_14(n32_32_buffer_1_row_14), .Row_15(n32_32_buffer_1_row_15),
    .Row_16(n32_32_buffer_1_row_16), .Row_17(n32_32_buffer_1_row_17), .Row_18(n32_32_buffer_1_row_18),
    .Row_19(n32_32_buffer_1_row_19), .Row_20(n32_32_buffer_1_row_20), .Row_21(n32_32_buffer_1_row_21),
    .Row_22(n32_32_buffer_1_row_22), .Row_23(n32_32_buffer_1_row_23), .Row_24(n32_32_buffer_1_row_24),
    .Row_25(n32_32_buffer_1_row_25), .Row_26(n32_32_buffer_1_row_26), .Row_27(n32_32_buffer_1_row_27),
    .Row_28(n32_32_buffer_1_row_28), .Row_29(n32_32_buffer_1_row_29), .Row_30(n32_32_buffer_1_row_30),
    .Row_31(n32_32_buffer_1_row_31), .Row_0_2(generation_buffer_1_row_0_2),
    .Row_1_2(generation_buffer_1_row_1_2), .Row_2_2(generation_buffer_1_row_2_2),
    .Row_3_2(generation_buffer_1_row_3_2), .Row_4_2(generation_buffer_1_row_4_2),
    .Row_5_2(generation_buffer_1_row_5_2), .Row_6_2(generation_buffer_1_row_6_2),
    .Row_7_2(generation_buffer_1_row_7_2), .Row_8_2(generation_buffer_1_row_8_2),
    .Row_9_2(generation_buffer_1_row_9_2), .Row_10_2(generation_buffer_1_row_10_2),
    .Row_11_2(generation_buffer_1_row_11_2), .Row_12_2(generation_buffer_1_row_12_2),
    .Row_13_2(generation_buffer_1_row_13_2), .Row_14_2(generation_buffer_1_row_14_2),
    .Row_15_2(generation_buffer_1_row_15_2), .Row_16_2(generation_buffer_1_row_16_2),
    .Row_17_2(generation_buffer_1_row_17_2), .Row_18_2(generation_buffer_1_row_18_2),
    .Row_19_2(generation_buffer_1_row_19_2), .Row_20_2(generation_buffer_1_row_20_2),
    .Row_21_2(generation_buffer_1_row_21_2), .Row_22_2(generation_buffer_1_row_22_2),
    .Row_23_2(generation_buffer_1_row_23_2), .Row_24_2(generation_buffer_1_row_24_2),
    .Row_25_2(generation_buffer_1_row_25_2), .Row_26_2(generation_buffer_1_row_26_2),
    .Row_27_2(generation_buffer_1_row_27_2), .Row_28_2(generation_buffer_1_row_28_2),
    .Row_29_2(generation_buffer_1_row_29_2), .Row_30_2(generation_buffer_1_row_30_2),
    .Row_31_2(generation_buffer_1_row_31_2));
  Multiplexer #(.disabled(0), .enable("false")) multiplexer_4 (
    .in0(clock), .in1(update_generation), .out(multiplexer_4_out), .sel(playing));
  Decoder #(.disabled(0)) decoder_5 (.out0(update_generation), .sel(in_out), .en(and_5_out));  // open: out1
  Decoder #(.disabled(0)) decoder_6 (.out0(decoder_6_out0), .sel(in_out), .en(and_6_out));  // open: out1
  Decoder #(.disabled(0)) decoder_7 (.out1(decoder_7_out1), .sel(in_out), .en(and_7_out));  // open: out0
  Comparator comparator_8 (.a(IOaddr), .b(8'hfa), .eq(comparator_8_eq));  // open: gt, lt
  and and_5 (and_5_out, comparator_8_eq, IOsel);
  Comparator comparator_9 (.a(IOaddr), .b(8'hf4), .eq(comparator_9_eq));  // open: gt, lt
  and and_6 (and_6_out, comparator_9_eq, IOsel);
  Comparator comparator_10 (.a(IOaddr), .b(8'hf1), .eq(comparator_10_eq));  // open: gt, lt
  and and_7 (and_7_out, comparator_10_eq, IOsel);
  // Probe on cdm_8_mark5_1_p4
  // Probe on cdm_8_mark5_1_p1
  // Probe on cdm_8_mark5_1_p2
  Clock clock_1 (.out(clock));
  and and_8 (IOsel, not_25_out, clock, data);
  not not_23 (not_23_out, not_23_out);
  not not_24 (not_24_out, not_24_out);
  env_constructor env_constructor_1 (
    .Row_0(generation_buffer_1_row_0_2), .Row_1(generation_buffer_1_row_1_2),
    .Row_2(generation_buffer_1_row_2_2), .Row_3(generation_buffer_1_row_3_2),
    .Row_4(generation_buffer_1_row_4_2), .Row_5(generation_buffer_1_row_5_2),
    .Row_6(generation_buffer_1_row_6_2), .Row_7(generation_buffer_1_row_7_2),
    .Row_8(generation_buffer_1_row_8_2), .Row_9(generation_buffer_1_row_9_2),
    .Row_10(generation_buffer_1_row_10_2), .Row_11(generation_buffer_1_row_11_2),
    .Row_12(generation_buffer_1_row_12_2), .Row_13(generation_buffer_1_row_13_2),
    .Row_14(generation_buffer_1_row_14_2), .Row_15(generation_buffer_1_row_15_2),
    .Row_16(generation_buffer_1_row_16_2), .Row_17(generation_buffer_1_row_17_2),
    .Row_18(generation_buffer_1_row_18_2), .Row_19(generation_buffer_1_row_19_2),
    .Row_20(generation_buffer_1_row_20_2), .Row_21(generation_buffer_1_row_21_2),
    .Row_22(generation_buffer_1_row_22_2), .Row_23(generation_buffer_1_row_23_2),
    .Row_24(generation_buffer_1_row_24_2), .Row_25(generation_buffer_1_row_25_2),
    .Row_26(generation_buffer_1_row_26_2), .Row_27(generation_buffer_1_row_27_2),
    .Row_28(generation_buffer_1_row_28_2), .Row_29(generation_buffer_1_row_29_2),
    .Row_30(generation_buffer_1_row_30_2), .Row_31(generation_buffer_1_row_31_2),
    .Is_byte_env__null(is_null_byte), .Y__row_index(multiplexer_2_out), .X__bit_index(multiplexer_3_out),
    .Is_row_env__null(is_row_null), .Sum(env_sum), .Bit(selected_bit));
  // Probe on cdm_8_mark5_1_p5
  // Probe on cdm_8_mark5_1_p6
  // Probe on cdm_8_mark5_1_p8
  // Probe on cdm_8_mark5_1_p7
  not not_25 (not_25_out, comparator_11_lt);
  // CdM_8_mark5 cdm_8_mark5_1: pin names not known; wires that end beside it: cdm_8_mark5_1_p1, cdm_8_mark5_1_p2, clock, cdm_8_mark5_1_p4, cdm_8_mark5_1_p5, cdm_8_mark5_1_p6, cdm_8_mark5_1_p7, cdm_8_mark5_1_p8, cdm_8_mark5_1_p9, mem, in_out, IOaddr, cdm_8_mark5_1_p13, cdm_8_mark5_1_p14
  assign bus = not_26_out ? cdm_8_mark5_1_p13 : 8'bz;  // Controlled_Buffer controlled_buffer_5
  not not_26 (not_26_out, in_out);
  assign cdm_8_mark5_1_p14 = in_out ? bus : 8'bz;  // Controlled_Buffer controlled_buffer_6
  and and_9 (RAM, comparator_11_lt, data);
  assign not_27_out = ~survival_input;  // NOT_Gate not_27, 8 bits wide
  not not_28 (not_28_out, setting);
  LED led_4 (.in(selected_bit));
  // Probe on env_sum
  Decoder #(.disabled(0)) decoder_8 (.out0(code), .out1(data), .sel(cdm_8_mark5_1_p9), .en(mem));
  Register register_6 (.D(not_27_out), .Q(register_6_q), .clk(xnor_3_out));  // open: en, clr
  xnor xnor_3 (xnor_3_out, not_28_out, setting);
  // Probe on IOaddr
  Comparator #(.mode("unsigned")) comparator_11 (.a(IOaddr), .b(8'hf0), .lt(comparator_11_lt));  // open: gt, eq
  Decoder #(.disabled(0)) decoder_9 (.out1(decoder_9_out1), .sel(in_out), .en(and_10_out));  // open: out0
  assign bus = decoder_9_out1 ? {{7{1'b0}}, selected_bit} : 8'bz;  // Controlled_Buffer controlled_buffer_7
  Decoder #(.disabled(0)) decoder_10 (.out1(decoder_10_out1), .sel(in_out), .en(and_11_out));  // open: out0
  assign bus = decoder_10_out1 ? register_6_q : 8'bz;  // Controlled_Buffer controlled_buffer_8
  bit_invertor bit_invertor_1 (
    .INPUT9(generation_buffer_1_row_8_2), .INPUT1(generation_buffer_1_row_0_2),
    .INPUT10(generation_buffer_1_row_9_2), .INPUT17(generation_buffer_1_row_16_2),
    .INPUT2(generation_buffer_1_row_1_2), .INPUT11(generation_buffer_1_row_10_2),
    .INPUT18(generation_buffer_1_row_17_2), .INPUT25(generation_buffer_1_row_24_2),
    .INPUT3(generation_buffer_1_row_2_2), .INPUT12(generation_buffer_1_row_11_2),
    .INPUT19(generation_buffer_1_row_18_2), .INPUT26(generation_buffer_1_row_25_2),
    .INPUT4(generation_buffer_1_row_3_2), .SWITCH(clock), .INPUT13(generation_buffer_1_row_12_2),
    .INPUT20(generation_buffer_1_row_19_2), .INPUT27(generation_buffer_1_row_26_2), .Y(multiplexer_2_out),
    .INPUT5(generation_buffer_1_row_4_2), .X(multiplexer_3_out), .INPUT14(generation_buffer_1_row_13_2),
    .INPUT21(generation_buffer_1_row_20_2), .INPUT28(generation_buffer_1_row_27_2),
    .INPUT6(generation_buffer_1_row_5_2), .INPUT15(generation_buffer_1_row_14_2),
    .INPUT22(generation_buffer_1_row_21_2), .INPUT29(generation_buffer_1_row_28_2),
    .INPUT7(generation_buffer_1_row_6_2), .INPUT16(generation_buffer_1_row_15_2),
    .INPUT23(generation_buffer_1_row_22_2), .INPUT30(generation_buffer_1_row_29_2),
    .INPUT8(generation_buffer_1_row_7_2), .INPUT24(generation_buffer_1_row_23_2),
    .INPUT31(generation_buffer_1_row_30_2), .INPUT32(generation_buffer_1_row_31_2),
    .OUTPUT1(bit_invertor_1_output1), .OUTPUT2(bit_invertor_1_output2), .OUTPUT3(bit_invertor_1_output3),
    .OUTPUT4(bit_invertor_1_output4), .OUTPUT5(bit_invertor_1_output5), .OUTPUT6(bit_invertor_1_output6),
    .OUTPUT7(bit_invertor_1_output7), .OUTPUT8(bit_invertor_1_output8), .OUTPUT9(bit_invertor_1_output9),
    .OUTPUT10(bit_invertor_1_output10), .OUTPUT11(bit_invertor_1_output11),
    .OUTPUT12(bit_invertor_1_output12), .OUTPUT13(bit_invertor_1_output13),
    .OUTPUT14(bit_invertor_1_output14), .OUTPUT15(bit_invertor_1_output15),
    .OUTPUT16(bit_invertor_1_output16), .OUTPUT17(bit_invertor_1_output17),
    .OUTPUT18(bit_invertor_1_output18), .OUTPUT19(bit_invertor_1_output19),
    .OUTPUT20(bit_invertor_1_output20), .OUTPUT21(bit_invertor_1_output21),
    .OUTPUT22(bit_invertor_1_output22), .OUTPUT23(bit_invertor_1_output23),
    .OUTPUT24(bit_invertor_1_output24), .OUTPUT25(bit_invertor_1_output25),
    .OUTPUT26(bit_invertor_1_output26), .OUTPUT27(bit_invertor_1_output27),
    .OUTPUT28(bit_invertor_1_output28), .OUTPUT29(bit_invertor_1_output29),
    .OUTPUT30(bit_invertor_1_output30), .OUTPUT31(bit_invertor_1_output31), .OUTPUT32(bit_invertor_1_output32));  // open: CHANGED_STRING
  Comparator comparator_12 (.a(IOaddr), .b(8'hf5), .eq(comparator_12_eq));  // open: gt, lt
  and and_10 (and_10_out, comparator_12_eq, IOsel);
  Comparator comparator_13 (.a(IOaddr), .b(8'hf2), .eq(comparator_13_eq));  // open: gt, lt
  and and_11 (and_11_out, comparator_13_eq, IOsel);
  // Probe on bus
  ROM rom_1 (.addr(IOaddr), .data(bus), .sel(code));
  RAM ram_1 (.addr(IOaddr), .data(bus), .sel(RAM), .clk(clock), .ld(in_out));  // open: clr
  DotMatrix #(.inputtype("row"), .matrixcols(32), .matrixrows(32)) dotmatrix_1 (
    .row0(bit_invertor_1_output1), .row1(bit_invertor_1_output2), .row2(bit_invertor_1_output3),
    .row3(bit_invertor_1_output4), .row4(bit_invertor_1_output5), .row5(bit_invertor_1_output6),
    .row6(bit_invertor_1_output7), .row7(bit_invertor_1_output8), .row8(bit_invertor_1_output9),
    .row9(bit_invertor_1_output10), .row10(bit_invertor_1_output11), .row11(bit_invertor_1_output12),
    .row12(bit_invertor_1_output13), .row13(bit_invertor_1_output14), .row14(bit_invertor_1_output15),
    .row15(bit_invertor_1_output16), .row16(bit_invertor_1_output17), .row17(bit_invertor_1_output18),
    .row18(bit_invertor_1_output19), .row19(bit_invertor_1_output20), .row20(bit_invertor_1_output21),
    .row21(bit_invertor_1_output22), .row22(bit_invertor_1_output23), .row23(bit_invertor_1_output24),
    .row24(bit_invertor_1_output25), .row25(bit_invertor_1_output26), .row26(bit_invertor_1_output27),
    .row27(bit_invertor_1_output28), .row28(bit_invertor_1_output29), .row29(bit_invertor_1_output30),
    .row30(bit_invertor_1_output31), .row31(bit_invertor_1_output32));
  not not_29 (not_29_out, not_29_out);
  assign bus = decoder_11_out1 ? env_sum : 8'bz;  // Controlled_Buffer controlled_buffer_9
  Comparator comparator_14 (.a(IOaddr), .b(8'hf6), .eq(comparator_14_eq));  // open: gt, lt
  Decoder #(.disabled(0)) decoder_11 (.out1(decoder_11_out1), .sel(in_out), .en(and_12_out));  // open: out0
  and and_12 (and_12_out, comparator_14_eq, IOsel);
  not not_30 (not_30_out, not_30_out);
  assign bus = decoder_12_out1 ? {{7{1'b0}}, is_row_null} : 8'bz;  // Controlled_Buffer controlled_buffer_10
  Decoder #(.disabled(0)) decoder_12 (.out1(decoder_12_out1), .sel(in_out), .en(and_13_out));  // open: out0
  Comparator comparator_15 (.a(IOaddr), .b(8'hf7), .eq(comparator_15_eq));  // open: gt, lt
  and and_13 (and_13_out, comparator_15_eq, IOsel);
  not not_31 (not_31_out, not_31_out);
  assign bus = decoder_13_out1 ? {{7{1'b0}}, is_null_byte} : 8'bz;  // Controlled_Buffer controlled_buffer_11
  Comparator comparator_16 (.a(IOaddr), .b(8'hf8), .eq(comparator_16_eq));  // open: gt, lt
  Decoder #(.disabled(0)) decoder_13 (.out1(decoder_13_out1), .sel(in_out), .en(and_14_out));  // open: out0
  and and_14 (and_14_out, comparator_16_eq, IOsel);

  // Other names for the same wires on the sheet: birth_cond[7:0] = birth_input; IOdata[7:0] = bus; rd_wr = in_out;
  //   survival_cond[7:0] = survival_input

  // Notes on the sheet:
  //   Keyboard
  //   DEV I/O REGS.
  //   ROW READ / WRITE
  //   (read only thus CdM -> buffer)
  //   PROCESSED CELL
  //   READ ONLY INPUTS
  //   (immutable game state)
  //   Cell 0xff (CPU status)
  //   Cell 0xf3 (Y - row)
  //   Cell 0xf5 (invert signal)
  //   Cell 0xf0 (state)
  //   waiting for start
  //   reading field
  //   processing field
  //   Cell 0xf6 (uodate generation buffer)
  //   Cell 0xf4 (X - bit)
  //   Cell 0xf1 (birth conditions)
  //   Structure of I/O bus
  //   Cell 0xfa (bit value)
  //   Cell 0xf2 (survival conditions)
  //   Harvard Architecture
  //   Minimal IO cell address
  //   contents of rom_1 (hex, n*v repeats v):
  //   ee 35 d2 8 d1 0 18 a e0 11 88 b3 95 1d 8a ee 7 4 d7 d3 8 f e0 21 d2 1 42 a6 8d 98 8b ee 15 d7 5 e1
  //   29 d2 60 ee 2b d2 68 88 12 ba a e0 34 d0 f9 a0 d7 cd 50 d0 ff d1 40 a1 d1 f0 b4 0 e0 3e d1 50 a4 d1
  //   f1 b4 d1 60 d6 13 d1 f2 b4 d1 68 d6 13 d0 fa a0 d0 ff d1 42 a1 d3 1f c3 d0 f3 a3 d3 f7 bf f e1 9c d1
  //   1f d3 4 c3 d0 f4 a1 d0 f8 b0 0 e1 95 d3 8 c1 d0 f4 a1 d0 f6 b0 d1 f5 b5 0 e0 88 d6 22 ee 8e 5 e0 8e
  //   d0 f9 a0 c5 89 8b e1 77 ee 98 d0 f8 11 c7 8b e1 6b c7 8b e5 5d ee 53 d4
  //   Cell 0xfb (env. sum)
  //   Cell 0xfc (is null rows env.)
  //   Cell 0xfd (is null byte env.)
endmodule

module env_constructor (
  input  [4:0] Y__row_index,
  input  [4:0] X__bit_index,
  input  [31:0] Row_0,
  input  [31:0] Row_1,
  input  [31:0] Row_2,
  input  [31:0] Row_3,
  input  [31:0] Row_4,
  input  [31:0] Row_5,
  input  [31:0] Row_6,
  input  [31:0] Row_7,
  input  [31:0] Row_8,
  input  [31:0] Row_9,
  input  [31:0] Row_10,
  input  [31:0] Row_11,
  input  [31:0] Row_12,
  input  [31:0] Row_13,
  input  [31:0] Row_14,
  input  [31:0] Row_15,
  input  [31:0] Row_16,
  input  [31:0] Row_17,
  input  [31:0] Row_18,
  input  [31:0] Row_19,
  input  [31:0] Row_20,
  input  [31:0] Row_21,
  input  [31:0] Row_22,
  input  [31:0] Row_23,
  input  [31:0] Row_24,
  input  [31:0] Row_25,
  input  [31:0] Row_26,
  input  [31:0] Row_27,
  input  [31:0] Row_28,
  input  [31:0] Row_29,
  input  [31:0] Row_30,
  input  [31:0] Row_31,
  output Is_row_env__null,
  output Is_byte_env__null,
  output [7:0] Sum,
  output Bit
);

  wire nor_1_out, nor_2_out, nor_3_out, nor_4_out, nor_5_out, nor_6_out, nor_7_out, nor_8_out, nor_9_out;
  wire [4:0] adder_1_out, adder_2_out, adder_3_out;
  wire [7:0] adder_4_out, adder_5_out, adder_6_out, adder_7_out, adder_8_out, adder_9_out, adder_10_out;
  wire [31:0] multiplexer_1_out, multiplexer_2_out, multiplexer_3_out, shifter_1_out, shifter_2_out,
       shifter_3_out;

  Adder #(.width(5)) adder_1 (.a({5{1'b1}}), .b(Y__row_index), .out(adder_1_out));  // open: cin, cout
  Adder #(.width(5)) adder_2 (.a(Y__row_index), .b(5'b00001), .out(adder_2_out));  // open: cin, cout
  Multiplexer #(.select(5), .width(32), .enable("false")) multiplexer_1 (
    .in0(Row_0), .in1(Row_1), .in2(Row_2), .in3(Row_3), .in4(Row_4), .in5(Row_5), .in6(Row_6), .in7(Row_7),
    .in8(Row_8), .in9(Row_9), .in10(Row_10), .in11(Row_11), .in12(Row_12), .in13(Row_13), .in14(Row_14),
    .in15(Row_15), .in16(Row_16), .in17(Row_17), .in18(Row_18), .in19(Row_19), .in20(Row_20), .in21(Row_21),
    .in22(Row_22), .in23(Row_23), .in24(Row_24), .in25(Row_25), .in26(Row_26), .in27(Row_27), .in28(Row_28),
    .in29(Row_29), .in30(Row_30), .in31(Row_31), .out(multiplexer_1_out), .sel(adder_1_out));
  Multiplexer #(.select(5), .width(32), .enable("false")) multiplexer_2 (
    .in0(Row_0), .in1(Row_1), .in2(Row_2), .in3(Row_3), .in4(Row_4), .in5(Row_5), .in6(Row_6), .in7(Row_7),
    .in8(Row_8), .in9(Row_9), .in10(Row_10), .in11(Row_11), .in12(Row_12), .in13(Row_13), .in14(Row_14),
    .in15(Row_15), .in16(Row_16), .in17(Row_17), .in18(Row_18), .in19(Row_19), .in20(Row_20), .in21(Row_21),
    .in22(Row_22), .in23(Row_23), .in24(Row_24), .in25(Row_25), .in26(Row_26), .in27(Row_27), .in28(Row_28),
    .in29(Row_29), .in30(Row_30), .in31(Row_31), .out(multiplexer_2_out), .sel(Y__row_index));
  Multiplexer #(.select(5), .width(32), .enable("false")) multiplexer_3 (
    .in0(Row_0), .in1(Row_1), .in2(Row_2), .in3(Row_3), .in4(Row_4), .in5(Row_5), .in6(Row_6), .in7(Row_7),
    .in8(Row_8), .in9(Row_9), .in10(Row_10), .in11(Row_11), .in12(Row_12), .in13(Row_13), .in14(Row_14),
    .in15(Row_15), .in16(Row_16), .in17(Row_17), .in18(Row_18), .in19(Row_19), .in20(Row_20), .in21(Row_21),
    .in22(Row_22), .in23(Row_23), .in24(Row_24), .in25(Row_25), .in26(Row_26), .in27(Row_27), .in28(Row_28),
    .in29(Row_29), .in30(Row_30), .in31(Row_31), .out(multiplexer_3_out), .sel(adder_2_out));
  // Probe on adder_3_out
  Adder #(.width(5)) adder_3 (.a(X__bit_index), .b({5{1'b1}}), .out(adder_3_out));  // open: cin, cout
  Adder adder_4 (.a({8{1'b0}}), .b({8{1'b0}}), .out(adder_4_out), .cin(shifter_3_out[2]));  // open: cout
  Shifter #(.width(32), .shift("rr")) shifter_1 (.in(multiplexer_1_out), .\dist (adder_3_out), .out(shifter_1_out));
  Shifter #(.width(32), .shift("rr")) shifter_2 (
    .in(multiplexer_2_out), .\dist (adder_3_out), .out({shifter_2_out[31:2], Bit, shifter_2_out[0]}));
  Shifter #(.width(32), .shift("rr")) shifter_3 (.in(multiplexer_3_out), .\dist (adder_3_out), .out(shifter_3_out));
  Adder adder_5 (.a({8{1'b0}}), .b(adder_4_out), .out(adder_5_out), .cin(shifter_3_out[1]));  // open: cout
  Adder adder_6 (.a(adder_5_out), .b({8{1'b0}}), .out(adder_6_out), .cin(shifter_3_out[0]));  // open: cout
  Adder adder_7 (.a({8{1'b0}}), .b(adder_6_out), .out(adder_7_out), .cin(shifter_2_out[2]));  // open: cout
  Adder adder_8 (.a(adder_7_out), .b({8{1'b0}}), .out(adder_8_out), .cin(shifter_2_out[0]));  // open: cout
  Adder adder_9 (.a({8{1'b0}}), .b(adder_8_out), .out(adder_9_out), .cin(shifter_1_out[2]));  // open: cout
  nor nor_1 (nor_1_out, shifter_1_out[31], shifter_1_out[30], shifter_1_out[29], shifter_1_out[28], shifter_1_out[27], shifter_1_out[26], shifter_1_out[25], shifter_1_out[24], shifter_1_out[23], shifter_1_out[22], shifter_1_out[21], shifter_1_out[20], shifter_1_out[19], shifter_1_out[18], shifter_1_out[17], shifter_1_out[16], shifter_1_out[14], shifter_1_out[13], shifter_1_out[12], shifter_1_out[11], shifter_1_out[10], shifter_1_out[9], shifter_1_out[8], shifter_1_out[7], shifter_1_out[6], shifter_1_out[5], shifter_1_out[4], shifter_1_out[3], shifter_1_out[2], shifter_1_out[1], shifter_1_out[0], shifter_1_out[15]);
  nor nor_2 (nor_2_out, shifter_2_out[31], shifter_2_out[30], shifter_2_out[29], shifter_2_out[28], shifter_2_out[27], shifter_2_out[26], shifter_2_out[25], shifter_2_out[24], shifter_2_out[23], shifter_2_out[22], shifter_2_out[21], shifter_2_out[20], shifter_2_out[19], shifter_2_out[18], shifter_2_out[17], shifter_2_out[16], shifter_2_out[14], shifter_2_out[13], shifter_2_out[12], shifter_2_out[11], shifter_2_out[10], shifter_2_out[9], shifter_2_out[8], shifter_2_out[7], shifter_2_out[6], shifter_2_out[5], shifter_2_out[4], shifter_2_out[3], shifter_2_out[2], Bit, shifter_2_out[0], shifter_2_out[15]);
  nor nor_3 (nor_3_out, shifter_3_out[31], shifter_3_out[30], shifter_3_out[29], shifter_3_out[28], shifter_3_out[27], shifter_3_out[26], shifter_3_out[25], shifter_3_out[24], shifter_3_out[23], shifter_3_out[22], shifter_3_out[21], shifter_3_out[20], shifter_3_out[19], shifter_3_out[18], shifter_3_out[17], shifter_3_out[16], shifter_3_out[14], shifter_3_out[13], shifter_3_out[12], shifter_3_out[11], shifter_3_out[10], shifter_3_out[9], shifter_3_out[8], shifter_3_out[7], shifter_3_out[6], shifter_3_out[5], shifter_3_out[4], shifter_3_out[3], shifter_3_out[2], shifter_3_out[1], shifter_3_out[0], shifter_3_out[15]);
  Adder adder_10 (.a(adder_9_out), .b({8{1'b0}}), .out(adder_10_out), .cin(shifter_1_out[1]));  // open: cout
  Adder adder_11 (.a({8{1'b0}}), .b(adder_10_out), .out(Sum), .cin(shifter_1_out[0]));  // open: cout
  and and_1 (Is_row_env__null, nor_1_out, nor_2_out, nor_3_out);
  nor nor_4 (nor_4_out, shifter_1_out[31], shifter_1_out[30], shifter_1_out[29], shifter_1_out[28], shifter_1_out[27], shifter_1_out[26], shifter_1_out[25]);
  nor nor_5 (nor_5_out, shifter_2_out[31], shifter_2_out[30], shifter_2_out[29], shifter_2_out[28], shifter_2_out[27], shifter_2_out[26], shifter_2_out[25]);
  nor nor_6 (nor_6_out, shifter_3_out[31], shifter_3_out[30], shifter_3_out[29], shifter_3_out[28], shifter_3_out[27], shifter_3_out[26], shifter_3_out[25]);
  nor nor_7 (nor_7_out, shifter_1_out[2], shifter_1_out[1], shifter_1_out[0]);
  nor nor_8 (nor_8_out, shifter_2_out[2], Bit, shifter_2_out[0]);
  nor nor_9 (nor_9_out, shifter_3_out[2], shifter_3_out[1], shifter_3_out[0]);
  and and_2 (Is_byte_env__null, nor_7_out, nor_4_out, nor_8_out, nor_5_out, nor_9_out, nor_6_out);

  // Other names for the same wires on the sheet: row0[31:0] = Row_0; row1[31:0] = Row_1; row2[31:0] = Row_2;
  //   row3[31:0] = Row_3; row4[31:0] = Row_4; row5[31:0] = Row_5; row6[31:0] = Row_6; row7[31:0] = Row_7;
  //   row8[31:0] = Row_8; row9[31:0] = Row_9; row10[31:0] = Row_10; row11[31:0] = Row_11; row12[31:0] = Row_12;
  //   row13[31:0] = Row_13; row14[31:0] = Row_14; row15[31:0] = Row_15; row16[31:0] = Row_16; row17[31:0] = Row_17;
  //   row18[31:0] = Row_18; row19[31:0] = Row_19; row20[31:0] = Row_20; row21[31:0] = Row_21; row22[31:0] = Row_22;
  //   row23[31:0] = Row_23; row24[31:0] = Row_24; row25[31:0] = Row_25; row26[31:0] = Row_26; row27[31:0] = Row_27;
  //   row28[31:0] = Row_28; row29[31:0] = Row_29; row30[31:0] = Row_30; row31[31:0] = Row_31
endmodule

module generation_buffer (
  input  Save_generation_trigger,
  input  [31:0] Row_0,
  input  [31:0] Row_1,
  input  [31:0] Row_2,
  input  [31:0] Row_3,
  input  [31:0] Row_4,
  input  [31:0] Row_5,
  input  [31:0] Row_6,
  input  [31:0] Row_7,
  input  [31:0] Row_8,
  input  [31:0] Row_9,
  input  [31:0] Row_10,
  input  [31:0] Row_11,
  input  [31:0] Row_12,
  input  [31:0] Row_13,
  input  [31:0] Row_14,
  input  [31:0] Row_15,
  input  [31:0] Row_16,
  input  [31:0] Row_17,
  input  [31:0] Row_18,
  input  [31:0] Row_19,
  input  [31:0] Row_20,
  input  [31:0] Row_21,
  input  [31:0] Row_22,
  input  [31:0] Row_23,
  input  [31:0] Row_24,
  input  [31:0] Row_25,
  input  [31:0] Row_26,
  input  [31:0] Row_27,
  input  [31:0] Row_28,
  input  [31:0] Row_29,
  input  [31:0] Row_30,
  input  [31:0] Row_31,
  output [31:0] Row_0_2,
  output [31:0] Row_1_2,
  output [31:0] Row_2_2,
  output [31:0] Row_3_2,
  output [31:0] Row_4_2,
  output [31:0] Row_5_2,
  output [31:0] Row_6_2,
  output [31:0] Row_7_2,
  output [31:0] Row_8_2,
  output [31:0] Row_9_2,
  output [31:0] Row_10_2,
  output [31:0] Row_11_2,
  output [31:0] Row_12_2,
  output [31:0] Row_13_2,
  output [31:0] Row_14_2,
  output [31:0] Row_15_2,
  output [31:0] Row_16_2,
  output [31:0] Row_17_2,
  output [31:0] Row_18_2,
  output [31:0] Row_19_2,
  output [31:0] Row_20_2,
  output [31:0] Row_21_2,
  output [31:0] Row_22_2,
  output [31:0] Row_23_2,
  output [31:0] Row_24_2,
  output [31:0] Row_25_2,
  output [31:0] Row_26_2,
  output [31:0] Row_27_2,
  output [31:0] Row_28_2,
  output [31:0] Row_29_2,
  output [31:0] Row_30_2,
  output [31:0] Row_31_2
);

  Register #(.width(32)) register_1 (.D(Row_0), .Q(Row_0_2), .clk(Save_generation_trigger));  // open: en, clr
  Register #(.width(32)) register_2 (.D(Row_1), .Q(Row_1_2), .clk(Save_generation_trigger));  // open: en, clr
  Register #(.width(32)) register_3 (.D(Row_2), .Q(Row_2_2), .clk(Save_generation_trigger));  // open: en, clr
  Register #(.width(32)) register_4 (.D(Row_3), .Q(Row_3_2), .clk(Save_generation_trigger));  // open: en, clr
  Register #(.width(32)) register_5 (.D(Row_4), .Q(Row_4_2), .clk(Save_generation_trigger));  // open: en, clr
  Register #(.width(32)) register_6 (.D(Row_5), .Q(Row_5_2), .clk(Save_generation_trigger));  // open: en, clr
  Register #(.width(32)) register_7 (.D(Row_6), .Q(Row_6_2), .clk(Save_generation_trigger));  // open: en, clr
  Register #(.width(32)) register_8 (.D(Row_7), .Q(Row_7_2), .clk(Save_generation_trigger));  // open: en, clr
  Register #(.width(32)) register_9 (.D(Row_8), .Q(Row_8_2), .clk(Save_generation_trigger));  // open: en, clr
  Register #(.width(32)) register_10 (.D(Row_9), .Q(Row_9_2), .clk(Save_generation_trigger));  // open: en, clr
  Register #(.width(32)) register_11 (.D(Row_10), .Q(Row_10_2), .clk(Save_generation_trigger));  // open: en, clr
  Register #(.width(32)) register_12 (.D(Row_11), .Q(Row_11_2), .clk(Save_generation_trigger));  // open: en, clr
  Register #(.width(32)) register_13 (.D(Row_12), .Q(Row_12_2), .clk(Save_generation_trigger));  // open: en, clr
  Register #(.width(32)) register_14 (.D(Row_13), .Q(Row_13_2), .clk(Save_generation_trigger));  // open: en, clr
  Register #(.width(32)) register_15 (.D(Row_14), .Q(Row_14_2), .clk(Save_generation_trigger));  // open: en, clr
  Register #(.width(32)) register_16 (.D(Row_15), .Q(Row_15_2), .clk(Save_generation_trigger));  // open: en, clr
  Register #(.width(32)) register_17 (.D(Row_16), .Q(Row_16_2), .clk(Save_generation_trigger));  // open: en, clr
  Register #(.width(32)) register_18 (.D(Row_17), .Q(Row_17_2), .clk(Save_generation_trigger));  // open: en, clr
  Register #(.width(32)) register_19 (.D(Row_18), .Q(Row_18_2), .clk(Save_generation_trigger));  // open: en, clr
  Register #(.width(32)) register_20 (.D(Row_19), .Q(Row_19_2), .clk(Save_generation_trigger));  // open: en, clr
  Register #(.width(32)) register_21 (.D(Row_20), .Q(Row_20_2), .clk(Save_generation_trigger));  // open: en, clr
  Register #(.width(32)) register_22 (.D(Row_21), .Q(Row_21_2), .clk(Save_generation_trigger));  // open: en, clr
  Register #(.width(32)) register_23 (.D(Row_22), .Q(Row_22_2), .clk(Save_generation_trigger));  // open: en, clr
  Register #(.width(32)) register_24 (.D(Row_23), .Q(Row_23_2), .clk(Save_generation_trigger));  // open: en, clr
  Register #(.width(32)) register_25 (.D(Row_24), .Q(Row_24_2), .clk(Save_generation_trigger));  // open: en, clr
  Register #(.width(32)) register_26 (.D(Row_25), .Q(Row_25_2), .clk(Save_generation_trigger));  // open: en, clr
  Register #(.width(32)) register_27 (.D(Row_26), .Q(Row_26_2), .clk(Save_generation_trigger));  // open: en, clr
  Register #(.width(32)) register_28 (.D(Row_27), .Q(Row_27_2), .clk(Save_generation_trigger));  // open: en, clr
  Register #(.width(32)) register_29 (.D(Row_28), .Q(Row_28_2), .clk(Save_generation_trigger));  // open: en, clr
  Register #(.width(32)) register_30 (.D(Row_29), .Q(Row_29_2), .clk(Save_generation_trigger));  // open: en, clr
  Register #(.width(32)) register_31 (.D(Row_30), .Q(Row_30_2), .clk(Save_generation_trigger));  // open: en, clr
  Register #(.width(32)) register_32 (.D(Row_31), .Q(Row_31_2), .clk(Save_generation_trigger));  // open: en, clr
endmodule

module tiny_bit_invertor (
  input  [4:0] Y__row_index,
  input  [4:0] X__bit_index,
  input  [31:0] Row_0,
  input  [31:0] Row_1,
  input  [31:0] Row_2,
  input  [31:0] Row_3,
  input  [31:0] Row_4,
  input  [31:0] Row_5,
  input  [31:0] Row_6,
  input  [31:0] Row_7,
  input  [31:0] Row_8,
  input  [31:0] Row_9,
  input  [31:0] Row_10,
  input  [31:0] Row_11,
  input  [31:0] Row_12,
  input  [31:0] Row_13,
  input  [31:0] Row_14,
  input  [31:0] Row_15,
  input  [31:0] Row_16,
  input  [31:0] Row_17,
  input  [31:0] Row_18,
  input  [31:0] Row_19,
  input  [31:0] Row_20,
  input  [31:0] Row_21,
  input  [31:0] Row_22,
  input  [31:0] Row_23,
  input  [31:0] Row_24,
  input  [31:0] Row_25,
  input  [31:0] Row_26,
  input  [31:0] Row_27,
  input  [31:0] Row_28,
  input  [31:0] Row_29,
  input  [31:0] Row_30,
  input  [31:0] Row_31,
  output [31:0] Row_with_inverted_bit
);

  wire [31:0] multiplexer_1_out, shifter_1_out;

  Multiplexer #(.select(5), .width(32), .enable("false")) multiplexer_1 (
    .in0(Row_0), .in1(Row_1), .in2(Row_2), .in3(Row_3), .in4(Row_4), .in5(Row_5), .in6(Row_6), .in7(Row_7),
    .in8(Row_8), .in9(Row_9), .in10(Row_10), .in11(Row_11), .in12(Row_12), .in13(Row_13), .in14(Row_14),
    .in15(Row_15), .in16(Row_16), .in17(Row_17), .in18(Row_18), .in19(Row_19), .in20(Row_20), .in21(Row_21),
    .in22(Row_22), .in23(Row_23), .in24(Row_24), .in25(Row_25), .in26(Row_26), .in27(Row_27), .in28(Row_28),
    .in29(Row_29), .in30(Row_30), .in31(Row_31), .out(multiplexer_1_out), .sel(Y__row_index));
  // Probe on shifter_1_out
  Shifter #(.width(32), .shift("rl")) shifter_1 (.in(32'h1), .\dist (X__bit_index), .out(shifter_1_out));
  assign Row_with_inverted_bit = shifter_1_out ^ multiplexer_1_out;  // XOR_Gate xor_1, 32 bits wide

  // Other names for the same wires on the sheet: row0[31:0] = Row_0; row1[31:0] = Row_1; row2[31:0] = Row_2;
  //   row3[31:0] = Row_3; row4[31:0] = Row_4; row5[31:0] = Row_5; row6[31:0] = Row_6; row7[31:0] = Row_7;
  //   row8[31:0] = Row_8; row9[31:0] = Row_9; row10[31:0] = Row_10; row11[31:0] = Row_11; row12[31:0] = Row_12;
  //   row13[31:0] = Row_13; row14[31:0] = Row_14; row15[31:0] = Row_15; row16[31:0] = Row_16; row17[31:0] = Row_17;
  //   row18[31:0] = Row_18; row19[31:0] = Row_19; row20[31:0] = Row_20; row21[31:0] = Row_21; row22[31:0] = Row_22;
  //   row23[31:0] = Row_23; row24[31:0] = Row_24; row25[31:0] = Row_25; row26[31:0] = Row_26; row27[31:0] = Row_27;
  //   row28[31:0] = Row_28; row29[31:0] = Row_29; row30[31:0] = Row_30; row31[31:0] = Row_31
endmodule
